# Fritzing sketch Raspberry Pi Hat and Motor Control (saved by Fritzing 0.9.3b)
perfboards: 2

parts:
  Part1_(PWM_Driver) = 16-Channel 12-bit PWM Servo Driver - I2C [part_number=815]
  J3_5v_Rail = Screw terminal - 2 pins [package=THT]
  J4_6v_Rail = Screw terminal - 2 pins [package=THT]
  Raspberry_Pi1 = Raspberry Pi B+
  J3_(LED_Driver_Connector) = female pin header, 2 pins [form="♀ (female)"]
  J3_RPi_5v = Screw terminal - 2 pins [package=THT]
  L298N1_(Rear) = L298N DC motor driver
  L298N2_(Front) = L298N DC motor driver
  J3_(PWM_Board_Connector_-_Source) = female pin header, 4 pins [form="♀ (female)"]
  J3_(PWM_Board_Connector_-_Target) = female pin header, 4 pins [form="♀ (female)"]
  J3_(Shutdown_Button_Connector) = female pin header, 2 pins [form="♀ (female)"]
  S1 = Round Pushbutton
  J1_(Front_Right_Motor_Driver_Connector) = female pin header, 3 pins [form="♀ (female)"]
  J3_(Front_Left_Motor_Driver_Connector) = female pin header, 3 pins [form="♀ (female)"]
  J2_(Rear_Left_Motor_Driver_Connector) = female pin header, 3 pins [form="♀ (female)"]
  J4_(Rear_Right_Motor_Driver_Connector) = female pin header, 3 pins [form="♀ (female)"]
  J5_(Servos_Connector) = female pin header, 5 pins [form="♀ (female)"]
  J6_(Front_Motor_Direction_Connector_-_Target) = female pin header, 4 pins [form="♀ (female)"]
  J7_(Rear_Motor_Direction_Connector_-_Target) = female pin header, 4 pins [form="♀ (female)"]
  J3_(Wattmeter_Connector) = female pin header, 4 pins [form="♀ (female)"]
  J8_(Rear_Motor_Direction_Connector_-_Source) = female pin header, 4 pins [form="♀ (female)"]
  J9_(Front_Motor_Direction_Connector_-_Source) = female pin header, 4 pins [form="♀ (female)"]
  J10 = Piezo Speaker
  J3_(Piezo_Speaker_Connector) = female pin header, 2 pins [form="♀ (female)"]

nets:
  6V: Part1_(PWM_Driver).PWRIN, J4_6v_Rail.pin2
  GND: Part1_(PWM_Driver).GND, J3_5v_Rail.pin1, J4_6v_Rail.pin1, Raspberry_Pi1.GND, J3_RPi_5v.pin1, J3_(PWM_Board_Connector_-_Source).pin2, J3_(PWM_Board_Connector_-_Target).pin2, J5_(Servos_Connector).pin2, J3_(Wattmeter_Connector).pin2
  N1: Part1_(PWM_Driver).PWM6, J5_(Servos_Connector).pin3
  N2: Part1_(PWM_Driver).PWM5, J5_(Servos_Connector).pin4
  N3: Part1_(PWM_Driver).PWM4, J5_(Servos_Connector).pin5
  N4: Part1_(PWM_Driver).5.0V, J5_(Servos_Connector).pin1
  5V: Part1_(PWM_Driver).VCC, J3_5v_Rail.pin2, Raspberry_Pi1.5V, J3_RPi_5v.pin2, J3_(PWM_Board_Connector_-_Source).pin1, J3_(PWM_Board_Connector_-_Target).pin1, J3_(Wattmeter_Connector).pin1
  N5: Part1_(PWM_Driver).SDA, Raspberry_Pi1.GPIO2, J3_(PWM_Board_Connector_-_Source).pin4, J3_(PWM_Board_Connector_-_Target).pin4, J3_(Wattmeter_Connector).pin4
  N6: Part1_(PWM_Driver).SCL, Raspberry_Pi1.GPIO3, J3_(PWM_Board_Connector_-_Source).pin3, J3_(PWM_Board_Connector_-_Target).pin3, J3_(Wattmeter_Connector).pin3
  N7: Part1_(PWM_Driver).PWM15, L298N1_(Rear).ENA, J3_(Front_Left_Motor_Driver_Connector).pin3
  N8: Part1_(PWM_Driver).PWM14, L298N1_(Rear).ENB, J1_(Front_Right_Motor_Driver_Connector).pin1
  N9: Part1_(PWM_Driver).PWM13, L298N2_(Front).ENB, J4_(Rear_Right_Motor_Driver_Connector).pin3
  N10: Part1_(PWM_Driver).PWM12, L298N2_(Front).ENA, J2_(Rear_Left_Motor_Driver_Connector).pin1
  3V3: Raspberry_Pi1.3v3, Raspberry_Pi1.3V3, J3_(LED_Driver_Connector).pin2
  N11: Raspberry_Pi1.GPIO17, L298N1_(Rear).IN1, J3_(Front_Left_Motor_Driver_Connector).pin2, J6_(Front_Motor_Direction_Connector_-_Target).pin4, J9_(Front_Motor_Direction_Connector_-_Source).pin1
  N12: Raspberry_Pi1.GPIO27, L298N2_(Front).IN4, J4_(Rear_Right_Motor_Driver_Connector).pin2, J7_(Rear_Motor_Direction_Connector_-_Target).pin4, J8_(Rear_Motor_Direction_Connector_-_Source).pin1
  N13: Raspberry_Pi1.GPIO5, L298N1_(Rear).IN4, J1_(Front_Right_Motor_Driver_Connector).pin2, J6_(Front_Motor_Direction_Connector_-_Target).pin1, J9_(Front_Motor_Direction_Connector_-_Source).pin4
  N14: Raspberry_Pi1.GPIO6, L298N1_(Rear).IN3, J1_(Front_Right_Motor_Driver_Connector).pin3, J6_(Front_Motor_Direction_Connector_-_Target).pin2, J9_(Front_Motor_Direction_Connector_-_Source).pin3
  N15: Raspberry_Pi1.GPIO13, J10.pin2, J3_(Piezo_Speaker_Connector).pin2
  N16: Raspberry_Pi1.GPIO19, L298N2_(Front).IN1, J2_(Rear_Left_Motor_Driver_Connector).pin2, J7_(Rear_Motor_Direction_Connector_-_Target).pin1, J8_(Rear_Motor_Direction_Connector_-_Source).pin4
  N17: Raspberry_Pi1.GPIO26, J3_(Shutdown_Button_Connector).pin2, S1.leg0
  N18: Raspberry_Pi1.GPIO21, L298N2_(Front).IN3, J4_(Rear_Right_Motor_Driver_Connector).pin1, J7_(Rear_Motor_Direction_Connector_-_Target).pin3, J8_(Rear_Motor_Direction_Connector_-_Source).pin2
  N19: Raspberry_Pi1.GPIO20, L298N2_(Front).IN2, J2_(Rear_Left_Motor_Driver_Connector).pin3, J7_(Rear_Motor_Direction_Connector_-_Target).pin2, J8_(Rear_Motor_Direction_Connector_-_Source).pin3
  N20: Raspberry_Pi1.GPIO16, L298N1_(Rear).IN2, J3_(Front_Left_Motor_Driver_Connector).pin1, J6_(Front_Motor_Direction_Connector_-_Target).pin3, J9_(Front_Motor_Direction_Connector_-_Source).pin2
  N21: Raspberry_Pi1.GPIO18, J3_(LED_Driver_Connector).pin1
  N22: J3_(Shutdown_Button_Connector).pin1, S1.leg1, J10.pin1, J3_(Piezo_Speaker_Connector).pin1

custom parts:
  16-Channel 12-bit PWM Servo Driver - I2C: You want to make a cool robot, maybe a hexapod walker, or maybe just a piece of art with a lot of moving parts. Or maybe you want to drive a lot of LEDs with precise PWM output. Using only two pins, control 16 free-running PWM outputs! You can even chain up 62 breakouts to control up to 992 PWM outputs.
  L298N DC motor driver: 2x DC motor driver with 78M05 positive voltage regulator (7..35 V) L298N: max 46 V, 2 A Set 5 V Enable jumper to enable 5 V regultor (needed for the L298N) and +5 V output at screw terminal or supply external +5 V at screw terminal Set ENA and/or ENB to +5 V to enable motor permanently or supply ENA and/or ENB with PWM signal IN1 and IN2 set rotation directory for motor A (OUT1/OUT2) IN2 and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
