# Fritzing sketch Telepresence Bot Electronics (saved by Fritzing 0.9.3b)
perfboards: 3

parts:
  Part1_-_PWM_Driver = 16-Channel 12-bit PWM Servo Driver - I2C [part_number=815]
  Part0_-_Raspberry_Pi = Raspberry Pi B+
  J3_(LED_Driver_Connector) = female pin header, 2 pins [form="♀ (female)"]
  J3_RPi_5v = Screw terminal - 2 pins [package=THT]
  L298N1_(Rear) = L298N DC motor driver
  L298N2_(Front) = L298N DC motor driver
  J3_(PWM_Board_Connector_-_Source) = female pin header, 4 pins [form="♀ (female)"]
  J3_(PWM_Board_Connector_-_Target) = female pin header, 4 pins [form="♀ (female)"]
  J3_(Shutdown_Button_Connector) = female pin header, 2 pins [form="♀ (female)"]
  S1 = Round Pushbutton
  J1_(Front_Right_Motor_Driver_Connector) = female pin header, 3 pins [form="♀ (female)"]
  J3_(Front_Left_Motor_Driver_Connector) = female pin header, 3 pins [form="♀ (female)"]
  J2_(Rear_Left_Motor_Driver_Connector) = female pin header, 3 pins [form="♀ (female)"]
  J4_(Rear_Right_Motor_Driver_Connector) = female pin header, 3 pins [form="♀ (female)"]
  J5_(Servos_Connector) = female pin header, 5 pins [form="♀ (female)"]
  J6_(Front_Motor_Direction_Connector_-_Target) = female pin header, 4 pins [form="♀ (female)"]
  J7_(Rear_Motor_Direction_Connector_-_Target) = female pin header, 4 pins [form="♀ (female)"]
  J3_(Wattmeter_Connector) = female pin header, 4 pins [form="♀ (female)"]
  J8_(Rear_Motor_Direction_Connector_-_Source) = female pin header, 4 pins [form="♀ (female)"]
  J9_(Front_Motor_Direction_Connector_-_Source) = female pin header, 4 pins [form="♀ (female)"]
  J10 = Piezo Speaker
  Part1_-_WATT_Meter = INA219 High Side DC Current Sensor Breakout [part_number="DFRobot SEN0291"]
  Battery_Connector = Power plug
  VBATT = DC Power [voltage=11.1V]
  Part3_-_5v_Buck_Converter = RioRand LM2596
  Part2_-_12v_Boost_Converter = DC-DC 2-24V Step Up Booster [package=THT]
  U1_-_Main_Power_Switch = SWITCH-SPST-2 [package=switch-spst-vertical]
  U2_-_Emergency_Stop_Button = SWITCH-SPST-2 [package=switch-spst-vertical]
  Part3_-_5v_Buck_Converter1 = RioRand LM2596
  M1 = DC Motor
  M2 = DC Motor
  M3 = DC Motor
  M4 = DC Motor
  J11 = Basic Servo
  J12 = Basic Servo
  J13 = Basic Servo
  J5_(Servos_Connector)1 = female pin header, 5 pins [form="♀ (female)"]
  J5_(Servos_Connector)2 = male pin header, 3 pins [form="♂ (male)"]
  J5_(Servos_Connector)3 = male pin header, 3 pins [form="♂ (male)"]
  J5_(Servos_Connector)4 = male pin header, 3 pins [form="♂ (male)"]
  NEOPIXEL1 = Neopixel Strip -- White (60/m) [part_number=1138]
  Battery_Connector1 = Power plug
  LED2 = LED - 3mm [color="Blue (470nm)" package="3 mm [THT]"]
  LED1_(Power) = LED - 3mm [color="Red (633nm)" package="3 mm [THT]"]
  R1 = Resistor [tolerance=±5% resistance=68 package=THT]
  R2 = Resistor [tolerance=±5% resistance=15 package=THT]
  J3_(PWM_Board_Connector_-_Source)1 = female pin header, 3 pins [form="♀ (female)"]

nets:
  N1: Part1_-_PWM_Driver.PWRIN, Part3_-_5v_Buck_Converter1.Pin_3
  GND: Part1_-_PWM_Driver.GND, Part0_-_Raspberry_Pi.GND, J3_RPi_5v.pin1, L298N1_(Rear).GND, L298N2_(Front).GND, J3_(PWM_Board_Connector_-_Source).pin2, J3_(PWM_Board_Connector_-_Target).pin2, J3_(Shutdown_Button_Connector).pin1, S1.leg1, J5_(Servos_Connector).pin2, J3_(Wattmeter_Connector).pin2, J10.pin1, Part1_-_WATT_Meter.GND, Battery_Connector.GND, VBATT.V-, Part3_-_5v_Buck_Converter.Pin_2, Part3_-_5v_Buck_Converter.Pin_4, Part2_-_12v_Boost_Converter.pin2, Part2_-_12v_Boost_Converter.pin4, Part3_-_5v_Buck_Converter1.Pin_2, Part3_-_5v_Buck_Converter1.Pin_4, J11.gnd, J12.gnd, J13.gnd, J5_(Servos_Connector)1.pin1, J5_(Servos_Connector)2.pin1, J5_(Servos_Connector)3.pin1, J5_(Servos_Connector)4.pin1, NEOPIXEL1.GND, Battery_Connector1.GND, LED2.cathode, J3_(PWM_Board_Connector_-_Source)1.pin3
  N2: Part1_-_PWM_Driver.PWM6, J5_(Servos_Connector).pin3, J11.pulse, J5_(Servos_Connector)1.pin3, J5_(Servos_Connector)2.pin3
  N3: Part1_-_PWM_Driver.PWM5, J5_(Servos_Connector).pin4, J12.pulse, J5_(Servos_Connector)1.pin4, J5_(Servos_Connector)3.pin3
  N4: Part1_-_PWM_Driver.PWM4, J5_(Servos_Connector).pin5, J13.pulse, J5_(Servos_Connector)1.pin5, J5_(Servos_Connector)4.pin3
  VCC: Part1_-_PWM_Driver.5.0V, J5_(Servos_Connector).pin1, J11.vcc, J12.vcc, J13.vcc, J5_(Servos_Connector)1.pin2, J5_(Servos_Connector)2.pin2, J5_(Servos_Connector)3.pin2, J5_(Servos_Connector)4.pin2
  5V: Part1_-_PWM_Driver.VCC, Part0_-_Raspberry_Pi.5V, J3_RPi_5v.pin2, L298N1_(Rear).5V, L298N2_(Front).5V, J3_(PWM_Board_Connector_-_Source).pin1, J3_(PWM_Board_Connector_-_Target).pin1, J3_(Wattmeter_Connector).pin1, Part1_-_WATT_Meter.VCC, Part3_-_5v_Buck_Converter.Pin_3, NEOPIXEL1.+5V
  N5: Part1_-_PWM_Driver.SDA, Part0_-_Raspberry_Pi.GPIO2, J3_(PWM_Board_Connector_-_Source).pin4, J3_(PWM_Board_Connector_-_Target).pin4, J3_(Wattmeter_Connector).pin4, Part1_-_WATT_Meter.SDA
  N6: Part1_-_PWM_Driver.SCL, Part0_-_Raspberry_Pi.GPIO3, J3_(PWM_Board_Connector_-_Source).pin3, J3_(PWM_Board_Connector_-_Target).pin3, J3_(Wattmeter_Connector).pin3, Part1_-_WATT_Meter.SCL
  N7: Part1_-_PWM_Driver.PWM15, L298N1_(Rear).ENA, J3_(Front_Left_Motor_Driver_Connector).pin3
  N8: Part1_-_PWM_Driver.PWM14, L298N1_(Rear).ENB, J1_(Front_Right_Motor_Driver_Connector).pin1
  N9: Part1_-_PWM_Driver.PWM13, L298N2_(Front).ENB, J4_(Rear_Right_Motor_Driver_Connector).pin3
  N10: Part1_-_PWM_Driver.PWM12, L298N2_(Front).ENA, J2_(Rear_Left_Motor_Driver_Connector).pin1
  N11: Part0_-_Raspberry_Pi.3v3, R1.Pin_1, J3_(PWM_Board_Connector_-_Source)1.pin2
  N12: Part0_-_Raspberry_Pi.GPIO17, L298N1_(Rear).IN1, J3_(Front_Left_Motor_Driver_Connector).pin2, J6_(Front_Motor_Direction_Connector_-_Target).pin4, J9_(Front_Motor_Direction_Connector_-_Source).pin1
  N13: Part0_-_Raspberry_Pi.GPIO27, L298N2_(Front).IN4, J4_(Rear_Right_Motor_Driver_Connector).pin2, J7_(Rear_Motor_Direction_Connector_-_Target).pin4, J8_(Rear_Motor_Direction_Connector_-_Source).pin1
  N14: Part0_-_Raspberry_Pi.GPIO22, R2.Pin_1, J3_(PWM_Board_Connector_-_Source)1.pin1
  N15: Part0_-_Raspberry_Pi.GPIO5, L298N1_(Rear).IN4, J1_(Front_Right_Motor_Driver_Connector).pin2, J6_(Front_Motor_Direction_Connector_-_Target).pin1, J9_(Front_Motor_Direction_Connector_-_Source).pin4
  N16: Part0_-_Raspberry_Pi.GPIO6, L298N1_(Rear).IN3, J1_(Front_Right_Motor_Driver_Connector).pin3, J6_(Front_Motor_Direction_Connector_-_Target).pin2, J9_(Front_Motor_Direction_Connector_-_Source).pin3
  N17: Part0_-_Raspberry_Pi.GPIO13, J10.pin2
  N18: Part0_-_Raspberry_Pi.GPIO19, L298N2_(Front).IN1, J2_(Rear_Left_Motor_Driver_Connector).pin2, J7_(Rear_Motor_Direction_Connector_-_Target).pin1, J8_(Rear_Motor_Direction_Connector_-_Source).pin4
  N19: Part0_-_Raspberry_Pi.GPIO26, J3_(Shutdown_Button_Connector).pin2, S1.leg0
  N20: Part0_-_Raspberry_Pi.GPIO21, L298N2_(Front).IN3, J4_(Rear_Right_Motor_Driver_Connector).pin1, J7_(Rear_Motor_Direction_Connector_-_Target).pin3, J8_(Rear_Motor_Direction_Connector_-_Source).pin2
  N21: Part0_-_Raspberry_Pi.GPIO20, L298N2_(Front).IN2, J2_(Rear_Left_Motor_Driver_Connector).pin3, J7_(Rear_Motor_Direction_Connector_-_Target).pin2, J8_(Rear_Motor_Direction_Connector_-_Source).pin3
  N22: Part0_-_Raspberry_Pi.GPIO16, L298N1_(Rear).IN2, J3_(Front_Left_Motor_Driver_Connector).pin1, J6_(Front_Motor_Direction_Connector_-_Target).pin3, J9_(Front_Motor_Direction_Connector_-_Source).pin2
  N23: Part0_-_Raspberry_Pi.GPIO18, J3_(LED_Driver_Connector).pin1, NEOPIXEL1.DI
  N24: L298N1_(Rear).OUT1, M3.pin_2
  N25: L298N1_(Rear).OUT2, M3.pin_1
  N26: L298N1_(Rear).OUT3, M4.pin_2
  N27: L298N1_(Rear).OUT4, M4.pin_1
  12V: L298N1_(Rear).12V, L298N2_(Front).12V, U2_-_Emergency_Stop_Button.P
  N28: L298N2_(Front).OUT1, M1.pin_2
  N29: L298N2_(Front).OUT2, M1.pin_1
  N30: L298N2_(Front).OUT3, M2.pin_2
  N31: L298N2_(Front).OUT4, M2.pin_1
  N32: Part1_-_WATT_Meter.VIN-, Part2_-_12v_Boost_Converter.pin3
  N33: Part1_-_WATT_Meter.VIN+, U1_-_Main_Power_Switch.O
  VCC_2: Battery_Connector.VCC, VBATT.V+, U1_-_Main_Power_Switch.P, Battery_Connector1.VCC
  12V_2: Part3_-_5v_Buck_Converter.Pin_1, Part2_-_12v_Boost_Converter.pin1, U2_-_Emergency_Stop_Button.O, Part3_-_5v_Buck_Converter1.Pin_1
  N34: LED2.anode, R2.Pin_0
  N35: LED1_(Power).anode, R1.Pin_0

notes:
  Main Power
  5v Rail
  12v Rail
  Power Monitor
  6v Rail
  Emergency Stop
  3S (11.1v) Battery Input
  Speaker
  Raspberry Pi 4 & Prototyping Hat
  Soft Shutdown
  Rear Left
  Rear Right
  Front Right
  Front Left
  Front Motor Driver
  Rear Motor Driver
  PWM Generator
  Head Breakout
  Brake
  Pan
  Tilt
  LED Strip

custom parts:
  16-Channel 12-bit PWM Servo Driver - I2C: You want to make a cool robot, maybe a hexapod walker, or maybe just a piece of art with a lot of moving parts. Or maybe you want to drive a lot of LEDs with precise PWM output. Using only two pins, control 16 free-running PWM outputs! You can even chain up 62 breakouts to control up to 992 PWM outputs.
  L298N DC motor driver: 2x DC motor driver with 78M05 positive voltage regulator (7..35 V) L298N: max 46 V, 2 A Set 5 V Enable jumper to enable 5 V regultor (needed for the L298N) and +5 V output at screw terminal or supply external +5 V at screw terminal Set ENA and/or ENB to +5 V to enable motor permanently or supply ENA and/or ENB with PWM signal IN1 and IN2 set rotation directory for motor A (OUT1/OUT2) IN2 and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
  INA219 High Side DC Current Sensor Breakout: This breakout board will solve all your power-monitoring problems. Instead of struggling with two multimeters, you can just use the handy INA219B chip on this breakout to both measure both the high side voltage and DC current draw over I2C with 1% precision. Most current-measuring devices such as our current panel meter are only good for low side measuring. That means that unless you want to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
  DC-DC 2-24V Step Up Booster: Convertisseur DC-DC 2-24V 2A
  Neopixel Strip -- White (60/m): Neopixel Strip, White, 60 pixels per meter.
